# Fritzing sketch wiring (saved by Fritzing 1.0.4)

parts:
  M1 = RioRand LM2596
  Bat1 = battery_holder_single_18650
  Bat2 = battery_holder_single_18650
  S1 = SWITCH_SPDT [package=kps-1290]
  Raspberry_Pi_A1 = Raspberry Pi 4B
  LED1 = 7-SEGMENT-4DIGIT [package=7-segment-4digit]
  L298N1 = L298N DC motor driver
  L298N2 = L298N DC motor driver
  M2 = DC Motor [voltage_(max)=6V voltage_(min)=3V]
  M3 = DC Motor [voltage_(max)=6V voltage_(min)=3V]
  M4 = DC Motor [voltage_(max)=6V voltage_(min)=3V]
  M5 = DC Motor [voltage_(max)=6V voltage_(min)=3V]

nets:
  12V: M1.Pin_1, S1.O, LED1.6, L298N1.12V, L298N2.12V
  GND: M1.Pin_2, Bat1.+#0, LED1.2, L298N1.GND, L298N2.GND
  N1: M1.Pin_3, Raspberry_Pi_A1.5V
  N2: M1.Pin_4, Raspberry_Pi_A1.GND
  N3: Bat1.+#1, Bat2.+#0
  N4: Bat2.+#1, S1.S
  N5: Raspberry_Pi_A1.GPIO17, L298N2.ENB
  N6: Raspberry_Pi_A1.GPIO27, L298N2.IN4
  N7: Raspberry_Pi_A1.GPIO22, L298N2.IN3
  N8: Raspberry_Pi_A1.GPIO23, L298N1.ENA
  N9: Raspberry_Pi_A1.GPIO24, L298N1.IN1
  N10: Raspberry_Pi_A1.GPIO10, L298N2.IN2
  N11: Raspberry_Pi_A1.GPIO9, L298N2.IN1
  N12: Raspberry_Pi_A1.GPIO25, L298N1.IN2
  N13: Raspberry_Pi_A1.GPIO11, L298N2.ENA
  N14: Raspberry_Pi_A1.GPIO8, L298N1.IN3
  N15: Raspberry_Pi_A1.GPIO7, L298N1.IN4
  N16: Raspberry_Pi_A1.GPIO12, L298N1.ENB
  N17: L298N1.OUT1, M5.pin_2
  N18: L298N1.OUT2, M5.pin_1
  N19: L298N1.OUT3, M4.pin_2
  N20: L298N1.OUT4, M4.pin_1
  N21: L298N2.OUT1, M3.pin_2
  N22: L298N2.OUT2, M3.pin_1
  N23: L298N2.OUT3, M2.pin_2
  N24: L298N2.OUT4, M2.pin_1

notes:
  Both motor drivers are on dedicated Raspberry Pi Hat

custom parts:
  battery_holder_single_18650: single 18650 battery holder
  L298N DC motor driver: 2x DC motor driver with 78M05 positive voltage regulator (7..35 V) L298N: max 46 V, 2 A Set 5 V Enable jumper to enable 5 V regultor (needed for the L298N) and +5 V output at screw terminal or supply external +5 V at screw terminal Set ENA and/or ENB to +5 V to enable motor permanently or supply ENA and/or ENB with PWM signal IN1 and IN2 set rotation directory for motor A (OUT1/OUT2) IN2 and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
